// Logisim project ALU.circ as structural Verilog: 1 circuit, main circuit ALU
module ALU (
  input  [6:0] operation,
  input  [31:0] operand1,
  input  [31:0] operand2,
  input  [4:0] shamt,
  output zero,
  output [31:0] result
);

  wire beq_r, bgez_r, bgtz_r, blez_r, bne_r, comparator_1_gt, comparator_2_gt, multiplexer_5_out,
       multiplexer_6_out, multiplexer_7_out, multiplexer_8_out;
  wire [31:0] add_r, and_r, bit_extender_2_out, bit_extender_3_out, div_r, lui, mult_r, multiplexer_1_out,
       multiplexer_2_out, multiplexer_3_out, multiplexer_4_out, nor_r, or_r, sll_r, sllv_r, slt_r, sra_r,
       srl_r, srlv_r, sub_r, xor_r;
  wire [32:0] bit_extender_1_out;
  wire [32:32] shifter_5_out, shifter_6_out;

  Multiplexer #(.select(5), .width(32)) multiplexer_1 (
    .in0(sll_r), .in1({32{1'b0}}), .in2(srl_r), .in3(sra_r), .in4(sllv_r), .in5({32{1'b0}}), .in6(srlv_r),
    .in7({32{1'b0}}), .in8(operand1), .in9({32{1'b0}}), .in10({32{1'b0}}), .in11({32{1'b0}}),
    .in12({32{1'b0}}), .in13({32{1'b0}}), .in14({32{1'b0}}), .in15({32{1'b0}}), .in16({32{1'b0}}),
    .in17({32{1'b0}}), .in18({32{1'b0}}), .in19({32{1'b0}}), .in20({32{1'b0}}), .in21({32{1'b0}}),
    .in22({32{1'b0}}), .in23({32{1'b0}}), .in24(mult_r), .in25({32{1'b0}}), .in26(div_r), .in27({32{1'b0}}),
    .in28({32{1'b0}}), .in29({32{1'b0}}), .in30({32{1'b0}}), .in31(lui), .out(multiplexer_1_out),
    .sel(operation[4:0]));
  Multiplexer #(.select(5), .width(32)) multiplexer_2 (
    .in0(add_r), .in1(add_r), .in2(sub_r), .in3(sub_r), .in4(and_r), .in5(or_r), .in6(xor_r), .in7(nor_r),
    .in8({32{1'b0}}), .in9({32{1'b0}}), .in10(slt_r), .in11({32{1'b0}}), .in12({32{1'b0}}),
    .in13({32{1'b0}}), .in14({32{1'b0}}), .in15({32{1'b0}}), .in16({32{1'b0}}), .in17({32{1'b0}}),
    .in18({32{1'b0}}), .in19({32{1'b0}}), .in20({32{1'b0}}), .in21({32{1'b0}}), .in22({32{1'b0}}),
    .in23({32{1'b0}}), .in24({32{1'b0}}), .in25({32{1'b0}}), .in26({32{1'b0}}), .in27({32{1'b0}}),
    .in28({32{1'b0}}), .in29({32{1'b0}}), .in30({32{1'b0}}), .in31({32{1'b0}}), .out(multiplexer_2_out),
    .sel(operation[4:0]));
  Multiplexer #(.select(5), .width(32)) multiplexer_3 (
    .in0({32{1'b0}}), .in1({32{1'b0}}), .in2({32{1'b0}}), .in3({32{1'b0}}), .in4({32{1'b0}}),
    .in5({32{1'b0}}), .in6({32{1'b0}}), .in7({32{1'b0}}), .in8(add_r), .in9(add_r), .in10(slt_r),
    .in11({32{1'b0}}), .in12(and_r), .in13(or_r), .in14(xor_r), .in15(add_r), .in16({32{1'b0}}),
    .in17({32{1'b0}}), .in18({32{1'b0}}), .in19({32{1'b0}}), .in20({32{1'b0}}), .in21({32{1'b0}}),
    .in22({32{1'b0}}), .in23({32{1'b0}}), .in24({32{1'b0}}), .in25({32{1'b0}}), .in26({32{1'b0}}),
    .in27({32{1'b0}}), .in28({32{1'b0}}), .in29({32{1'b0}}), .in30({32{1'b0}}), .in31({32{1'b0}}),
    .out(multiplexer_3_out), .sel(operation[4:0]));
  Multiplexer #(.select(5), .width(32)) multiplexer_4 (
    .in0(add_r), .in1({32{1'b0}}), .in2({32{1'b0}}), .in3(add_r), .in4({32{1'b0}}), .in5({32{1'b0}}),
    .in6({32{1'b0}}), .in7({32{1'b0}}), .in8(add_r), .in9({32{1'b0}}), .in10({32{1'b0}}), .in11(add_r),
    .in12({32{1'b0}}), .in13({32{1'b0}}), .in14({32{1'b0}}), .in15({32{1'b0}}), .in16({32{1'b0}}),
    .in17({32{1'b0}}), .in18({32{1'b0}}), .in19({32{1'b0}}), .in20({32{1'b0}}), .in21({32{1'b0}}),
    .in22({32{1'b0}}), .in23({32{1'b0}}), .in24({32{1'b0}}), .in25({32{1'b0}}), .in26({32{1'b0}}),
    .in27({32{1'b0}}), .in28({32{1'b0}}), .in29({32{1'b0}}), .in30({32{1'b0}}), .in31({32{1'b0}}),
    .out(multiplexer_4_out), .sel(operation[4:0]));
  Multiplexer #(.select(2)) multiplexer_5 (
    .in0(1'b0), .in1(bgez_r), .in2(1'b0), .in3(1'b0), .out(multiplexer_5_out), .sel(operation[1:0]));
  Multiplexer #(.select(2)) multiplexer_6 (
    .in0(beq_r), .in1(bne_r), .in2(blez_r), .in3(bgtz_r), .out(multiplexer_6_out), .sel(operation[1:0]));
  Multiplexer multiplexer_7 (
    .in0(multiplexer_5_out), .in1(multiplexer_6_out), .out(multiplexer_7_out), .sel(operation[2]));
  Multiplexer #(.select(2)) multiplexer_8 (
    .in0(multiplexer_7_out), .in1(1'b0), .in2(1'b0), .in3(1'b0), .out(multiplexer_8_out), .sel(operation[4:3]));
  Multiplexer #(.select(2), .width(32)) multiplexer_9 (
    .in0(multiplexer_1_out), .in1(multiplexer_2_out), .in2(multiplexer_3_out), .in3(multiplexer_4_out),
    .out(result), .sel(operation[6:5]));
  Multiplexer #(.select(2)) multiplexer_10 (
    .in0(1'b0), .in1(1'b0), .in2(multiplexer_8_out), .in3(1'b0), .out(zero), .sel(operation[6:5]));
  assign bit_extender_1_out = {{1{1'b0}}, operand2};  // Bit_Extender bit_extender_1
  Adder #(.width(32)) adder_1 (.a(operand1), .b(operand2), .out(add_r));  // open: cin, cout
  Subtractor #(.width(32)) subtractor_1 (.a(operand1), .b(operand2), .out(sub_r));  // open: bin, bout
  assign and_r = operand1 & operand2;  // AND_Gate and_1, 32 bits wide
  assign or_r = operand1 | operand2;  // OR_Gate or_1, 32 bits wide
  assign xor_r = operand1 ^ operand2;  // XOR_Gate xor_1, 32 bits wide
  Multiplier #(.width(32)) multiplier_1 (.a(operand1), .b(operand2), .out(mult_r));  // open: cin, cout
  assign bit_extender_2_out = {{16{operand1[15]}}, operand1[15:0]};  // Bit_Extender bit_extender_2
  assign bit_extender_3_out = {{16{1'b0}}, operand1[31:16]};  // Bit_Extender bit_extender_3
  Divider #(.width(32)) divider_1 (
    .a(bit_extender_3_out), .b(operand2), .out(div_r), .upper(bit_extender_2_out));  // open: rem
  Shifter #(.width(32)) shifter_1 (.in(operand2), .\dist (5'b10000), .out(lui));
  Shifter #(.width(32)) shifter_2 (.in(operand2), .\dist (shamt), .out(sll_r));
  Shifter #(.shift("lr"), .width(32)) shifter_3 (.in(operand2), .\dist (shamt), .out(srl_r));
  Shifter #(.shift("ar"), .width(32)) shifter_4 (.in(operand2), .\dist (shamt), .out(sra_r));
  assign nor_r = ~(operand2 | operand1);  // NOR_Gate nor_1, 32 bits wide
  Shifter #(.width(33)) shifter_5 (.in(bit_extender_1_out), .\dist (operand1[5:0]), .out({shifter_5_out[32], sllv_r}));
  Shifter #(.shift("lr"), .width(33)) shifter_6 (
    .in(bit_extender_1_out), .\dist (operand1[5:0]), .out({shifter_6_out[32], srlv_r}));
  Comparator #(.width(32)) comparator_1 (.a(operand2), .b(operand1), .gt(comparator_1_gt), .eq(beq_r));  // open: lt
  not not_1 (bne_r, beq_r);
  Comparator #(.width(32)) comparator_2 (.a({32{1'b0}}), .b(operand1), .gt(comparator_2_gt), .lt(bgtz_r));  // open: eq
  assign slt_r = {{31{1'b0}}, comparator_1_gt};  // Bit_Extender bit_extender_4
  not not_2 (bgez_r, comparator_2_gt);
  not not_3 (blez_r, bgtz_r);

  // Other names for the same wires on the sheet: addr_r[31:0] = add_r; slti_r[31:0] = slt_r

  // Notes on the sheet:
  //   inputs
  //   outputs
  //   operations:
  //   all the operations should be added here with a tunnel and then connected to MUX
endmodule
