// Logisim project control_unit.circ as structural Verilog: 1 circuit, main circuit CU
module CU (
  input  [31:0] instruction,
  output ALUSrc,
  output RegDst,
  output Byte,
  output MemToReg,
  output [6:0] aluOp,
  output MemWrite,
  output Branch,
  output RegWrite,
  output [2:0] Jump
);

  wire adi, and_3_out, comparator_1_eq, comparator_2_eq, decoder_1_out1, decoder_1_out4, decoder_1_out5,
       decoder_1_out6, decoder_1_out7, decoder_2_out1, decoder_2_out2, decoder_2_out4, decoder_2_out5,
       decoder_2_out6, decoder_2_out7, decoder_2_out8, decoder_2_out12, nor_1_out, nor_2_out, nor_4_out,
       not_1_out, not_2_out, not_3_out, not_4_out, not_5_out, or_1_out, or_3_out;
  wire [5:0] multiplexer_1_out;

  not not_1 (not_1_out, RegDst);
  and and_1 (adi, not_1_out, comparator_1_eq);
  and and_2 (Jump[0], RegDst, comparator_2_eq);
  Comparator #(.width(6)) comparator_1 (.a(instruction[31:26]), .b(6'b001000), .eq(comparator_1_eq));  // open: gt, lt
  Comparator #(.width(6)) comparator_2 (.a(instruction[5:0]), .b(6'b001000), .eq(comparator_2_eq));  // open: gt, lt
  nor nor_1 (nor_1_out, instruction[31], instruction[30], instruction[29]);
  Decoder #(.select(3)) decoder_1 (
    .out1(decoder_1_out1), .out4(decoder_1_out4), .out5(decoder_1_out5), .out6(decoder_1_out6),
    .out7(decoder_1_out7), .sel(instruction[28:26]), .en(nor_1_out));  // open: out0, out2, out3
  not not_2 (not_2_out, instruction[31]);
  Decoder #(.select(5)) decoder_2 (
    .out1(decoder_2_out1), .out2(decoder_2_out2), .out3(Jump[1]), .out4(decoder_2_out4),
    .out5(decoder_2_out5), .out6(decoder_2_out6), .out7(decoder_2_out7), .out8(decoder_2_out8),
    .out12(decoder_2_out12), .sel(instruction[30:26]), .en(not_2_out));  // open: out0, out9, out10, out11, out13, out14, out15, out16, out17, out18, out19, out20, out21, out22, out23, out24, out25, out26, out27, out28, out29, out30, out31
  and and_3 (and_3_out, instruction[27], instruction[26]);
  nor nor_2 (nor_2_out, instruction[27], instruction[26]);
  nor nor_3 (RegDst, instruction[26], instruction[27], instruction[28], instruction[29], instruction[30], instruction[31]);
  not not_3 (not_3_out, instruction[30]);
  not not_4 (not_4_out, instruction[29]);
  not not_5 (not_5_out, instruction[28]);
  or or_1 (or_1_out, and_3_out, nor_2_out);
  and and_4 (MemToReg, instruction[31], not_3_out, not_4_out, not_5_out, or_1_out);
  or or_2 (Branch, decoder_1_out1, decoder_1_out4, decoder_1_out5, decoder_1_out6, decoder_1_out7);
  not not_6 (ALUSrc, RegDst);
  and and_5 (MemWrite, or_1_out, not_5_out, instruction[29], not_3_out, instruction[31]);
  nor nor_4 (nor_4_out, MemWrite, decoder_2_out1, decoder_2_out2, decoder_2_out4, decoder_2_out5, decoder_2_out6, decoder_2_out7, decoder_2_out8, decoder_2_out12);
  or or_3 (or_3_out, Jump[0], adi);
  and and_6 (Byte, instruction[31], not_3_out, not_5_out, nor_2_out);
  Multiplexer #(.width(6)) multiplexer_1 (
    .in0(instruction[31:26]), .in1(instruction[5:0]), .out(multiplexer_1_out), .sel(RegDst));
  xor xor_1 (RegWrite, or_3_out, nor_4_out);
  or or_4 (Jump[2], Jump[1], decoder_2_out2);
  assign aluOp = {{1{ALUSrc}}, multiplexer_1_out};  // Bit_Extender bit_extender_1

  // Other names for the same wires on the sheet: fu[5:0] = instruction[5:0]; op[5:0] = instruction[31:26];
  //   is_r = RegDst; jr = Jump[0]
endmodule
