// Logisim project cpu.circ as structural Verilog: 1 circuit, main circuit cpu
module cpu (
  input  in_1
);

  wire alu_1_zero, and_1_out, and_2_out, \byte , clk, cu_1_alusrc, cu_1_branch, cu_1_memwrite, cu_1_regdst,
       d_ff_1_q, jal, MemToReg, not_1_out, not_2_out, RegW;
  wire [2:0] cu_1_jump;
  wire [3:0] decoder_1_out0, multiplexer_7_out;
  wire [4:0] InstMem_memreaddata_2, multiplexer_1_out, multiplexer_3_out;
  wire [6:0] cu_1_aluop;
  wire [7:0] multiplexer_10_out;
  wire [27:0] InstMem_memreaddata, shifter_2_out;
  wire [31:0] adder_1_out, adder_2_out, alu_1_result, bit_extender_1_out, bit_extender_2_out,
       DataMem_memreaddata, multiplexer_2_out, multiplexer_4_out, multiplexer_5_out, multiplexer_6_out,
       multiplexer_8_out, multiplexer_11_out, multiplexer_12_out, PC_q, PC_res, RegisterFile_readdata1,
       RegisterFile_readdata2, shifter_1_out;
  wire [31:28] InstMem_memreaddata_3;

  Register #(.width(32)) PC (.D(PC_res), .clk(and_1_out), .Q(PC_q), .clr(in_1));  // open: en
  and and_1 (and_1_out, clk, ~in_1);  // AND_Gate
  Clock clock_1 (.out(clk));
  mem InstMem (
    .MemAddress(PC_q), .clk(clk),
    .MemReadData({InstMem_memreaddata_3, InstMem_memreaddata[27:11], InstMem_memreaddata_2, InstMem_memreaddata[5:0]}));  // open: MemWriteMask, MemWriteData
  Multiplexer #(.width(5)) multiplexer_1 (
    .in0(InstMem_memreaddata[20:16]), .in1(InstMem_memreaddata[15:11]), .out(multiplexer_1_out),
    .sel(cu_1_regdst));
  Multiplexer #(.width(32)) multiplexer_2 (.in0(multiplexer_12_out), .in1(PC_q), .out(multiplexer_2_out), .sel(jal));
  Multiplexer #(.width(5)) multiplexer_3 (.in0(multiplexer_1_out), .in1({5{1'b1}}), .out(multiplexer_3_out), .sel(jal));
  D_Flip_Flop #(.trigger("falling")) d_ff_1 (.D(RegW), .clk(clk), .Q(d_ff_1_q));  // open: Qn, preset, reset
  not not_1 (not_1_out, clk);
  CU cu_1 (
    .instruction({InstMem_memreaddata_3, InstMem_memreaddata[27:11], InstMem_memreaddata_2, InstMem_memreaddata[5:0]}),
    .ALUSrc(cu_1_alusrc), .RegDst(cu_1_regdst), .Byte(\byte ), .MemToReg(MemToReg), .aluOp(cu_1_aluop),
    .MemWrite(cu_1_memwrite), .Branch(cu_1_branch), .RegWrite(RegW), .Jump({cu_1_jump[2], jal, cu_1_jump[0]}));
  regfile RegisterFile (
    .ReadIndex1(InstMem_memreaddata[25:21]), .ReadIndex2(InstMem_memreaddata[20:16]),
    .WriteIndex(multiplexer_3_out), .WriteData(multiplexer_2_out), .RegWEn(d_ff_1_q), .clk(not_1_out),
    .ReadData1(RegisterFile_readdata1), .ReadData2(RegisterFile_readdata2));
  assign bit_extender_1_out = {{16{InstMem_memreaddata[15]}}, {InstMem_memreaddata[15:11], InstMem_memreaddata_2, InstMem_memreaddata[5:0]}};  // Bit_Extender bit_extender_1
  Multiplexer #(.width(32)) multiplexer_4 (
    .in0(RegisterFile_readdata2), .in1(bit_extender_1_out), .out(multiplexer_4_out), .sel(cu_1_alusrc));
  Adder #(.width(32)) adder_1 (.a(32'h4), .b(PC_q), .out(adder_1_out));  // open: cin, cout
  Shifter #(.width(32)) shifter_1 (.in(bit_extender_1_out), .\dist (5'b00010), .out(shifter_1_out));
  Adder #(.width(32)) adder_2 (.a(adder_1_out), .b(shifter_1_out), .out(adder_2_out));  // open: cin, cout
  Shifter #(.width(28)) shifter_2 (
    .in({InstMem_memreaddata[27:11], InstMem_memreaddata_2, InstMem_memreaddata[5:0]}), .\dist (5'b00010),
    .out(shifter_2_out));
  Multiplexer #(.width(32)) multiplexer_5 (
    .in0(adder_1_out), .in1(adder_2_out), .out(multiplexer_5_out), .sel(and_2_out));
  and and_2 (and_2_out, cu_1_branch, alu_1_zero);
  ALU alu_1 (
    .operation(cu_1_aluop), .operand1(RegisterFile_readdata1), .operand2(multiplexer_4_out),
    .shamt(InstMem_memreaddata_2), .zero(alu_1_zero), .result(alu_1_result));
  Decoder #(.enable("false"), .select(2)) decoder_1 (
    .out0(decoder_1_out0[0]), .out1(decoder_1_out0[1]), .out2(decoder_1_out0[2]), .out3(decoder_1_out0[3]),
    .sel(alu_1_result[1:0]));
  Multiplexer #(.width(32)) multiplexer_6 (
    .in0(multiplexer_5_out), .in1({adder_1_out[31:28], shifter_2_out}), .out(multiplexer_6_out),
    .sel(cu_1_jump[2]));
  Multiplexer #(.enable("true"), .width(4)) multiplexer_7 (
    .in0(4'b1111), .in1(decoder_1_out0), .out(multiplexer_7_out), .sel(\byte ), .en(cu_1_memwrite));
  Multiplexer #(.width(32)) multiplexer_8 (
    .in0(RegisterFile_readdata2),
    .in1({RegisterFile_readdata2[7:0], RegisterFile_readdata2[7:0], RegisterFile_readdata2[7:0], RegisterFile_readdata2[7:0]}),
    .out(multiplexer_8_out), .sel(\byte ));
  Multiplexer #(.width(32)) multiplexer_9 (
    .in0(multiplexer_6_out), .in1(alu_1_result), .out(PC_res), .sel(cu_1_jump[0]));
  not not_2 (not_2_out, clk);
  mem DataMem (
    .MemAddress(alu_1_result), .MemWriteMask(multiplexer_7_out), .MemWriteData(multiplexer_8_out),
    .clk(not_2_out), .MemReadData(DataMem_memreaddata));
  Multiplexer #(.select(2), .width(8)) multiplexer_10 (
    .in0(DataMem_memreaddata[7:0]), .in1(DataMem_memreaddata[15:8]), .in2(DataMem_memreaddata[23:16]),
    .in3(DataMem_memreaddata[31:24]), .out(multiplexer_10_out), .sel(alu_1_result[1:0]));
  Multiplexer #(.width(32)) multiplexer_11 (
    .in0(DataMem_memreaddata), .in1(bit_extender_2_out), .out(multiplexer_11_out), .sel(\byte ));
  assign bit_extender_2_out = {{24{1'b0}}, multiplexer_10_out};  // Bit_Extender bit_extender_2
  Multiplexer #(.width(32)) multiplexer_12 (
    .in0(alu_1_result), .in1(multiplexer_11_out), .out(multiplexer_12_out), .sel(MemToReg));
endmodule
