// Logisim project mem.circ as structural Verilog: 1 circuit, main circuit mem
module mem (
  input  [31:0] MemAddress,
  input  [3:0] MemWriteMask,
  input  [31:0] MemWriteData,
  input  clk,
  output [31:0] MemReadData
);

  wire not_1_out;

  not not_1 (not_1_out, clk);
  RAM #(.addrWidth(14), .trigger("falling")) DMEM_0 (
    .addr(MemAddress[15:2]), .we(MemWriteMask[0]), .oe(1'b1), .clk(not_1_out), .din(MemWriteData[7:0]),
    .dout(MemReadData[7:0]));
  RAM #(.addrWidth(14), .trigger("falling")) DMEM_1 (
    .addr(MemAddress[15:2]), .we(MemWriteMask[1]), .oe(1'b1), .clk(not_1_out), .din(MemWriteData[15:8]),
    .dout(MemReadData[15:8]));
  RAM #(.addrWidth(14), .trigger("falling")) DMEM_2 (
    .addr(MemAddress[15:2]), .we(MemWriteMask[2]), .oe(1'b1), .clk(not_1_out), .din(MemWriteData[23:16]),
    .dout(MemReadData[23:16]));
  RAM #(.addrWidth(14), .trigger("falling")) DMEM_3 (
    .addr(MemAddress[15:2]), .we(MemWriteMask[3]), .oe(1'b1), .clk(not_1_out), .din(MemWriteData[31:24]),
    .dout(MemReadData[31:24]));
endmodule
