// Logisim project regfile.circ as structural Verilog: 1 circuit, main circuit regfile
module regfile (
  input  [4:0] ReadIndex1,
  input  [4:0] ReadIndex2,
  input  [4:0] WriteIndex,
  input  [31:0] WriteData,
  input  RegWEn,
  input  clk,
  output [31:0] ReadData1,
  output [31:0] ReadData2
);

  wire we0, we1, we2, we3, we4, we5, we6, we7, we8, we9, we10, we11, we12, we13, we14, we15, we16, we17,
       we18, we19, we20, we21, we22, we23, we24, we25, we26, we27, we28, we29, we30, we31;
  wire [31:0] r0, r1, r2, r3, r4, r5, r6, r7, r8, r9, r10, r11, r12, r13, r14, r15, r16, r17, r18, r19, r20,
       r21, r22, r23, r24, r25, r26, r27, r28, r29, r30, r31;

  Register #(.trigger("falling"), .width(32)) register_1 (.D(WriteData), .en(1'b0), .clk(clk), .Q(r0));  // open: clr
  Register #(.trigger("falling"), .width(32)) register_2 (.D(WriteData), .en(we1), .clk(clk), .Q(r1));  // open: clr
  Register #(.trigger("falling"), .width(32)) register_3 (.D(WriteData), .en(we2), .clk(clk), .Q(r2));  // open: clr
  Register #(.trigger("falling"), .width(32)) register_4 (.D(WriteData), .en(we3), .clk(clk), .Q(r3));  // open: clr
  Register #(.trigger("falling"), .width(32)) register_5 (.D(WriteData), .en(we4), .clk(clk), .Q(r4));  // open: clr
  Register #(.trigger("falling"), .width(32)) register_6 (.D(WriteData), .en(we5), .clk(clk), .Q(r5));  // open: clr
  Register #(.trigger("falling"), .width(32)) register_7 (.D(WriteData), .en(we6), .clk(clk), .Q(r6));  // open: clr
  Register #(.trigger("falling"), .width(32)) register_8 (.D(WriteData), .en(we7), .clk(clk), .Q(r7));  // open: clr
  Register #(.trigger("falling"), .width(32)) register_9 (.D(WriteData), .en(we8), .clk(clk), .Q(r8));  // open: clr
  Register #(.trigger("falling"), .width(32)) register_10 (.D(WriteData), .en(we9), .clk(clk), .Q(r9));  // open: clr
  Register #(.trigger("falling"), .width(32)) register_11 (.D(WriteData), .en(we10), .clk(clk), .Q(r10));  // open: clr
  Register #(.trigger("falling"), .width(32)) register_12 (.D(WriteData), .en(we11), .clk(clk), .Q(r11));  // open: clr
  Register #(.trigger("falling"), .width(32)) register_13 (.D(WriteData), .en(we12), .clk(clk), .Q(r12));  // open: clr
  Register #(.trigger("falling"), .width(32)) register_14 (.D(WriteData), .en(we13), .clk(clk), .Q(r13));  // open: clr
  Register #(.trigger("falling"), .width(32)) register_15 (.D(WriteData), .en(we14), .clk(clk), .Q(r14));  // open: clr
  Register #(.trigger("falling"), .width(32)) register_16 (.D(WriteData), .en(we15), .clk(clk), .Q(r15));  // open: clr
  Register #(.trigger("falling"), .width(32)) register_17 (.D(WriteData), .en(we16), .clk(clk), .Q(r16));  // open: clr
  Register #(.trigger("falling"), .width(32)) register_18 (.D(WriteData), .en(we17), .clk(clk), .Q(r17));  // open: clr
  Register #(.trigger("falling"), .width(32)) register_19 (.D(WriteData), .en(we18), .clk(clk), .Q(r18));  // open: clr
  Register #(.trigger("falling"), .width(32)) register_20 (.D(WriteData), .en(we19), .clk(clk), .Q(r19));  // open: clr
  Register #(.trigger("falling"), .width(32)) register_21 (.D(WriteData), .en(we20), .clk(clk), .Q(r20));  // open: clr
  Register #(.trigger("falling"), .width(32)) register_22 (.D(WriteData), .en(we21), .clk(clk), .Q(r21));  // open: clr
  Register #(.trigger("falling"), .width(32)) register_23 (.D(WriteData), .en(we22), .clk(clk), .Q(r22));  // open: clr
  Register #(.trigger("falling"), .width(32)) register_24 (.D(WriteData), .en(we23), .clk(clk), .Q(r23));  // open: clr
  Register #(.trigger("falling"), .width(32)) register_25 (.D(WriteData), .en(we24), .clk(clk), .Q(r24));  // open: clr
  Register #(.trigger("falling"), .width(32)) register_26 (.D(WriteData), .en(we25), .clk(clk), .Q(r25));  // open: clr
  Register #(.trigger("falling"), .width(32)) register_27 (.D(WriteData), .en(we26), .clk(clk), .Q(r26));  // open: clr
  Register #(.trigger("falling"), .width(32)) register_28 (.D(WriteData), .en(we27), .clk(clk), .Q(r27));  // open: clr
  Register #(.trigger("falling"), .width(32)) register_29 (.D(WriteData), .en(we28), .clk(clk), .Q(r28));  // open: clr
  Register #(.trigger("falling"), .width(32)) register_30 (.D(WriteData), .en(we29), .clk(clk), .Q(r29));  // open: clr
  Register #(.trigger("falling"), .width(32)) register_31 (.D(WriteData), .en(we30), .clk(clk), .Q(r30));  // open: clr
  Register #(.trigger("falling"), .width(32)) register_32 (.D(WriteData), .en(we31), .clk(clk), .Q(r31));  // open: clr
  Multiplexer #(.select(5), .width(32)) multiplexer_1 (
    .in0(r0), .in1(r1), .in2(r2), .in3(r3), .in4(r4), .in5(r5), .in6(r6), .in7(r7), .in8(r8), .in9(r9),
    .in10(r10), .in11(r11), .in12(r12), .in13(r13), .in14(r14), .in15(r15), .in16(r16), .in17(r17),
    .in18(r18), .in19(r19), .in20(r20), .in21(r21), .in22(r22), .in23(r23), .in24(r24), .in25(r25),
    .in26(r26), .in27(r27), .in28(r28), .in29(r29), .in30(r30), .in31(r31), .out(ReadData1), .sel(ReadIndex1));
  Multiplexer #(.select(5), .width(32)) multiplexer_2 (
    .in0(r0), .in1(r1), .in2(r2), .in3(r3), .in4(r4), .in5(r5), .in6(r6), .in7(r7), .in8(r8), .in9(r9),
    .in10(r10), .in11(r11), .in12(r12), .in13(r13), .in14(r14), .in15(r15), .in16(r16), .in17(r17),
    .in18(r18), .in19(r19), .in20(r20), .in21(r21), .in22(r22), .in23(r23), .in24(r24), .in25(r25),
    .in26(r26), .in27(r27), .in28(r28), .in29(r29), .in30(r30), .in31(r31), .out(ReadData2), .sel(ReadIndex2));
  Decoder #(.select(5)) decoder_1 (
    .out0(we0), .out1(we1), .out2(we2), .out3(we3), .out4(we4), .out5(we5), .out6(we6), .out7(we7),
    .out8(we8), .out9(we9), .out10(we10), .out11(we11), .out12(we12), .out13(we13), .out14(we14),
    .out15(we15), .out16(we16), .out17(we17), .out18(we18), .out19(we19), .out20(we20), .out21(we21),
    .out22(we22), .out23(we23), .out24(we24), .out25(we25), .out26(we26), .out27(we27), .out28(we28),
    .out29(we29), .out30(we30), .out31(we31), .sel(WriteIndex), .en(RegWEn));

  // Notes on the sheet:
  //   INPUTS to your circuit
  //   OUTPUTS from your circuit
endmodule
